// Logisim project ODS_3.circ as structural Verilog: 2 circuits, main circuit ODS_3_1bit
module ODS_3_1bit (
  input  a,
  input  b,
  input  p_in,
  output S,
  output p_out
);

  wire not_1_out, not_2_out, not_3_out, or_1_out, or_2_out, or_3_out, or_4_out, or_5_out, or_6_out, or_7_out;

  not not_1 (not_1_out, a);
  not not_2 (not_2_out, b);
  not not_3 (not_3_out, p_in);
  or or_1 (or_1_out, a, b, p_in);
  or or_2 (or_2_out, a, not_2_out, not_3_out);
  or or_3 (or_3_out, not_1_out, b, not_3_out);
  or or_4 (or_4_out, not_1_out, not_2_out, p_in);
  or or_5 (or_5_out, a, b);
  or or_6 (or_6_out, a, p_in);
  or or_7 (or_7_out, b, p_in);
  and and_1 (S, or_1_out, or_2_out, or_3_out, or_4_out);
  and and_2 (p_out, or_5_out, or_6_out, or_7_out);
endmodule

module ODS_3_8bit (
  input  [7:0] in_1,
  input  [7:0] in_2,
  input  in_3,
  output [7:0] out_4
);

  wire ods_3_1bit_1_p_out, ods_3_1bit_2_p_out, ods_3_1bit_3_p_out, ods_3_1bit_4_p_out, ods_3_1bit_5_p_out,
       ods_3_1bit_6_p_out, ods_3_1bit_7_p_out, ods_3_1bit_8_p_out;

  ODS_3_1bit ods_3_1bit_1 (.a(in_1[0]), .b(in_2[0]), .p_in(1'b0), .S(out_4[0]), .p_out(ods_3_1bit_1_p_out));
  ODS_3_1bit ods_3_1bit_2 (
    .a(in_1[1]), .b(in_2[1]), .p_in(ods_3_1bit_1_p_out), .S(out_4[1]), .p_out(ods_3_1bit_2_p_out));
  ODS_3_1bit ods_3_1bit_3 (
    .a(in_1[2]), .b(in_2[2]), .p_in(ods_3_1bit_2_p_out), .S(out_4[2]), .p_out(ods_3_1bit_3_p_out));
  ODS_3_1bit ods_3_1bit_4 (
    .a(in_1[3]), .b(in_2[3]), .p_in(ods_3_1bit_3_p_out), .S(out_4[3]), .p_out(ods_3_1bit_4_p_out));
  ODS_3_1bit ods_3_1bit_5 (
    .a(in_1[4]), .b(in_2[4]), .p_in(ods_3_1bit_4_p_out), .S(out_4[4]), .p_out(ods_3_1bit_5_p_out));
  ODS_3_1bit ods_3_1bit_6 (
    .a(in_1[5]), .b(in_2[5]), .p_in(ods_3_1bit_5_p_out), .S(out_4[5]), .p_out(ods_3_1bit_6_p_out));
  ODS_3_1bit ods_3_1bit_7 (
    .a(in_1[6]), .b(in_2[6]), .p_in(ods_3_1bit_6_p_out), .S(out_4[6]), .p_out(ods_3_1bit_7_p_out));
  ODS_3_1bit ods_3_1bit_8 (
    .a(in_1[7]), .b(in_2[7]), .p_in(ods_3_1bit_7_p_out), .S(out_4[7]), .p_out(ods_3_1bit_8_p_out));
endmodule
