// Logisim project Сonverter_8421_n_1.circ as structural Verilog: 3 circuits, main circuit with_4_bit
module with_4_bit (
  input  x4,
  input  x3,
  input  x2,
  input  x1,
  output y1,
  output y2,
  output y3,
  output y4
);

  wire and_1_out, and_2_out, and_3_out, and_4_out, and_5_out, and_6_out, not_1_out, not_2_out;

  not not_1 (not_1_out, x3);
  not not_2 (not_2_out, x2);
  not not_3 (y1, x1);
  and and_1 (and_1_out, y1, x2);
  and and_2 (and_2_out, x1, not_2_out);
  and and_3 (and_3_out, not_1_out, x2, x1);
  and and_4 (and_4_out, x3, not_2_out);
  and and_5 (and_5_out, x3, y1);
  and and_6 (and_6_out, x3, x2, x1);
  or or_1 (y2, and_1_out, and_2_out);
  or or_2 (y3, and_3_out, and_4_out, and_5_out);
  or or_3 (y4, x4, and_6_out);
endmodule

module with_5_bit (
  input  x4,
  input  x3,
  input  x2,
  input  x1,
  output y1,
  output y2,
  output y3,
  output y4,
  output P
);

  wire and_1_out, and_2_out, and_3_out, and_4_out, and_5_out, and_6_out, and_7_out, and_8_out, and_9_out,
       and_10_out, not_1_out, not_2_out, not_3_out;

  not not_1 (not_1_out, x4);
  not not_2 (not_2_out, x3);
  not not_3 (not_3_out, x2);
  not not_4 (y1, x1);
  and and_1 (and_1_out, not_1_out, not_3_out, x1);
  and and_2 (and_2_out, x2, y1);
  and and_3 (and_3_out, x3, not_3_out, x1);
  and and_4 (and_4_out, not_2_out, x2, x1);
  and and_5 (and_5_out, x3, not_3_out);
  and and_6 (and_6_out, x3, y1);
  and and_7 (and_7_out, x3, x2, x1);
  and and_8 (and_8_out, x4, y1);
  and and_9 (and_9_out, x4, x2);
  and and_10 (and_10_out, x4, x3);
  and and_11 (P, x4, not_2_out, not_3_out, x1);
  or or_1 (y2, and_1_out, and_2_out, and_3_out);
  or or_2 (y3, and_4_out, and_5_out, and_6_out);
  or or_3 (y4, and_7_out, and_8_out, and_9_out, and_10_out);
endmodule

module bcd_8421_adder (
  input  [3:0] in_1,
  input  [3:0] in_2,
  output out_3,
  output [3:0] out_4
);

  wire adder_1_cout, and_1_out, and_2_out;
  wire [3:0] adder_1_out;

  Adder #(.width(4)) adder_1 (.a(in_1), .b(in_2), .out(adder_1_out), .cin(1'b1), .cout(adder_1_cout));
  Adder #(.width(4)) adder_2 (.a(adder_1_out), .b({1'b0, {2{out_3}}, 1'b0}), .out(out_4));  // open: cin, cout
  and and_1 (and_1_out, adder_1_out[3], adder_1_out[2]);
  and and_2 (and_2_out, adder_1_out[1], adder_1_out[3]);
  or or_1 (out_3, and_1_out, and_2_out, adder_1_cout);
endmodule
